# Fritzing sketch encoder (saved by Fritzing 0.9.3b)
circuit board: 8.46667cm x 5.64444cm
breadboards: 2

parts:
  RE1 = Rotary Encoder [package=THT]
  RE2 = Rotary Encoder [package=THT]
  R1 = Resistor [tolerance=±5% resistance=10k package="2512 [SMD]"]
  R2 = Resistor [tolerance=±5% resistance=10k package="2512 [SMD]"]
  Pro_Micro1 = Pro Micro
  Pro_Micro2 = Pro Micro

nets:
  N1: RE1.EncoderPinA, Pro_Micro1.D4
  N2: RE1.EncoderPinC, Pro_Micro1.GND
  N3: RE1.EncoderPinB, Pro_Micro1.D5
  N4: RE2.EncoderPinA, R1.Pin_0, Pro_Micro2.D4
  N5: RE2.EncoderPinB, R2.Pin_0, Pro_Micro2.D5
  N6: R1.Pin_1, R2.Pin_1, Pro_Micro2.VCC

custom parts:
  Pro Micro: The SparkFun Pro Micro is a complete USB-based microcontoller development system, in a very small footprint, capable of implementing many types of projects. All programming can be done via the USB port.
